// Logisim project abcco8r2.circ as structural Verilog
module CPU (
  output [7:0] Bus,
  output [7:0] MJA
);

  wire alu_new_1_cout_bout, button_1_out, button_2_out, button_3_out, button_4_out, button_5_out,
       button_6_out, button_7_out, button_8_out, button_9_out, button_10_out, Clear_out, clock_1_out,
       Clock_2_out, entry_1__0_2, entry_1__1_2, entry_1__2_2, entry_1__3_2, entry_1__4_2, entry_1__5_2,
       entry_1__6_2, entry_1__7_2, Interrupt_out, mctr_1_reading, mcu_1_clock_out, mcu_1_microcode_jump,
       mcu_1_program_counter_increment, mcu_1_register_read, mcu_1_register_write, mcu_1_waiting, not_1_out,
       or_1_out, or_2_out;
  wire [7:0] binary_to_bcd_2_p1, entry_1_value, mctr_1_address_2, mctr_1_instruction, mctr_1_mip_plus_plus,
       mctr_1_parameter, mcu_1_bus_out, mcu_1_register_select;
  wire [15:0] rom_1_data;

  MCTR mctr_1 (
    .Data(rom_1_data), .Address(MJA), .Jump(mcu_1_microcode_jump), .Clock(mcu_1_clock_out), .Reset(or_2_out),
    .MIP_Address(8'h2f), .Register(mcu_1_register_select), .Read(mcu_1_register_read),
    .Instruction(mctr_1_instruction), .Parameter(mctr_1_parameter), .Address_2(mctr_1_address_2),
    .MIP_plus_plus(mctr_1_mip_plus_plus), .Reading(mctr_1_reading));
  assign Bus = mctr_1_reading ? mctr_1_mip_plus_plus : 8'bz;  // Controlled_Buffer controlled_buffer_1
  Button button_1 (.out(button_1_out));
  Button button_2 (.out(button_2_out));
  Button button_3 (.out(button_3_out));
  Button button_4 (.out(button_4_out));
  LED led_1 (.in(entry_1__1_2));
  LED led_2 (.in(entry_1__0_2));
  ROM #(.dataWidth(16)) rom_1 (.addr(mctr_1_address_2), .data(rom_1_data));  // open: sel
  Button button_5 (.out(button_5_out));
  Button button_6 (.out(button_6_out));
  Button button_7 (.out(button_7_out));
  Button button_8 (.out(button_8_out));
  LED led_3 (.in(entry_1__2_2));
  LED led_4 (.in(entry_1__3_2));
  LED led_5 (.in(entry_1__5_2));
  LED led_6 (.in(entry_1__4_2));
  Clock clock_1 (.out(clock_1_out));
  Button Clock_2 (.out(Clock_2_out));
  Button Clear (.out(Clear_out));
  Button Interrupt (.out(Interrupt_out));
  Button button_9 (.out(button_9_out));
  Button button_10 (.out(button_10_out));
  Entry entry_1 (
    .Zero_all(button_3_out), .Enable(1'b1), .One_all(button_4_out), .Value(entry_1_value), ._0(button_2_out),
    ._1(button_1_out), ._2(button_6_out), ._3(button_8_out), ._4(button_5_out), ._5(button_7_out),
    ._6(button_10_out), ._7(button_9_out), ._0_2(entry_1__0_2), ._1_2(entry_1__1_2), ._2_2(entry_1__2_2),
    ._3_2(entry_1__3_2), ._4_2(entry_1__4_2), ._5_2(entry_1__5_2), ._6_2(entry_1__6_2), ._7_2(entry_1__7_2));
  LED led_7 (.in(entry_1__7_2));
  LED led_8 (.in(entry_1__6_2));
  or or_1 (or_1_out, clock_1_out, Clock_2_out);
  or or_2 (or_2_out, Clear_out, mcu_1_program_counter_increment);
  MCU mcu_1 (
    .Bus_in(Bus), .Parameter(mctr_1_parameter), .Cin_Bin(alu_new_1_cout_bout), .Interrupt(Interrupt_out),
    .Clock(or_1_out), .Clear(or_2_out), .Microcode(mctr_1_instruction), .Bus_out(mcu_1_bus_out),
    .Register_select(mcu_1_register_select), .Register_read(mcu_1_register_read), .Waiting(mcu_1_waiting),
    .Program_counter_increment(mcu_1_program_counter_increment), .Clock_out(mcu_1_clock_out),
    .Microcode_jump_address(MJA), .Microcode_jump(mcu_1_microcode_jump),
    .Register_write(mcu_1_register_write), .Address(mctr_1_address_2));
  ALU_NEW alu_new_1 (
    .Data(Bus), .Register_select(mcu_1_register_select), .Global_write(mcu_1_register_write),
    .Global_read(mcu_1_register_read), .Clear(or_2_out), .Output(Bus), .Cout_Bout(alu_new_1_cout_bout));  // open: Reading
  REG_BANK reg_bank_1 (
    .Bus_in(Bus), .Register_select(mcu_1_register_select), .Write(mcu_1_register_write),
    .Read(mcu_1_register_read), .Clear(or_2_out), .PCI(mcu_1_program_counter_increment), .Out(Bus));  // open: Is_reading
  Cache cache_1 (
    .Bus_in(Bus), .Register_select(mcu_1_register_select), .Clear(or_2_out), .Write(mcu_1_register_write),
    .Read(mcu_1_register_read), .Clock(mcu_1_clock_out), .Bus_out(Bus));  // open: Reading
  // Binary_to_BCD binary_to_bcd_1: pin names not known; wires that end beside it: Bus
  Hex_Digit_Display hex_digit_display_1 ();  // open: value, dp
  Hex_Digit_Display hex_digit_display_2 ();  // open: value, dp
  // Binary_to_BCD binary_to_bcd_2: pin names not known; wires that end beside it: binary_to_bcd_2_p1
  RBUF DBG (
    .Data_in(Bus), .Register_select(mcu_1_register_select), .Address({8{1'b1}}),
    .Write(mcu_1_register_write), .Clear(or_2_out), .Data_out(binary_to_bcd_2_p1));
  RRD rrd_1 (
    .Register_value(entry_1_value), .Register_address({8{1'b1}}), .Select(mcu_1_register_select),
    .Global_read(mcu_1_register_read), .Bus_out(Bus));  // open: Is_reading
  // Binary_to_BCD binary_to_bcd_3: pin names not known; wires that end beside it: mcu_1_program_counter_increment, mcu_1_clock_out, Bus, mcu_1_register_select, or_2_out, mcu_1_register_read, mcu_1_register_write, Bus, entry_1_value
  Hex_Digit_Display hex_digit_display_3 ();  // open: value, dp
  LED PCI (.in(mcu_1_program_counter_increment));
  LED Clock_in (.in(or_1_out));
  LED Clock_out (.in(mcu_1_clock_out));
  LED Waiting (.in(mcu_1_waiting));
  assign Bus = not_1_out ? mcu_1_bus_out : 8'bz;  // Controlled_Buffer controlled_buffer_2
  Pull_Resistor pull_resistor_1 (.node(Bus));
  not not_1 (not_1_out, mcu_1_register_read);
  LED MJ (.in(mcu_1_microcode_jump));
  LED Cout (.in(alu_new_1_cout_bout));
  Hex_Digit_Display hex_digit_display_4 ();  // open: value, dp
  Hex_Digit_Display hex_digit_display_5 ();  // open: value, dp
  Hex_Digit_Display hex_digit_display_6 ();  // open: value, dp
  Hex_Digit_Display hex_digit_display_7 ();  // open: value, dp
  Hex_Digit_Display hex_digit_display_8 ();  // open: value, dp
  Hex_Digit_Display hex_digit_display_9 ();  // open: value, dp

  // Notes on the sheet:
  //   contents of rom_1 (hex, n*v repeats v):
  //   0 900 1ff 220 900 1ff 221 300 222 223 120 436 121 436 120 210 121 211 309 212 113 220 30a 212 113
  //   221 2ff 120 210 30e 212 301 211 113 220 121 210 122 211 30d 212 113 222 2ff 800 433 210 123 211 113
  //   223 120 436 61b 122 2ff 900 123 2ff 900 a00
endmodule

module Cache (
  input  [7:0] Bus_in,
  input  [7:0] Register_select,
  input  Clear,
  input  Write,
  input  Read,
  input  Clock,
  output [7:0] Bus_out,
  output Reading
);

  wire equ_1_e_2, equ_2_e_2;
  wire [7:0] ram_1_data, register_1_q, register_2_q;

  EQU equ_1 (.A(Register_select), .B(8'h41), .E(Write), .E_2(equ_1_e_2));
  EQU equ_2 (.A(Register_select), .B(8'h40), .E(Write), .E_2(equ_2_e_2));
  EQU equ_3 (.A(Register_select), .B(8'h40), .E(Read), .E_2(Reading));
  Register register_1 (.D(Bus_in), .Q(register_1_q), .clk(equ_1_e_2), .clr(Clear));  // open: en
  Register register_2 (.D(Bus_in), .Q(register_2_q), .clk(equ_2_e_2), .clr(Clear));  // open: en
  assign Bus_out = Reading ? ram_1_data : 8'bz;  // Controlled_Buffer controlled_buffer_1
  RAM #(.bus("separate")) ram_1 (
    .addr(register_1_q), .din(register_2_q), .data(ram_1_data), .str(equ_2_e_2), .clk(Clock), .ld(Reading),
    .clr(Clear));  // open: sel
endmodule

module MCU (
  input  [7:0] Bus_in,
  input  [7:0] Parameter,
  input  Cin_Bin,
  input  Interrupt,
  input  Clock,
  input  Clear,
  input  [7:0] Microcode,
  input  [7:0] Address,
  output [7:0] Bus_out,
  output [7:0] Register_select,
  output Register_read,
  output Waiting,
  output Program_counter_increment,
  output Clock_out,
  output [7:0] Microcode_jump_address,
  output Microcode_jump,
  output Register_write
);

  wire comparator_1_eq, controlled_buffer_1_out, controlled_buffer_4_out, controlled_buffer_5_out,
       decoder_1_out1, decoder_1_out2, decoder_1_out3, decoder_1_out4, decoder_1_out5, decoder_1_out6,
       decoder_1_out7, decoder_1_out8, decoder_1_out9, decoder_1_out11, decoder_1_out12, decoder_1_out13,
       decoder_1_out14, decoder_1_out15, not_1_out, not_2_out, not_3_out, not_4_out, or_1_out, or_2_out,
       RS_out, s_r_ff_1_qn;
  wire [7:0] adder_1_out, multiplexer_1_out, multiplexer_3_out, multiplexer_4_out, multiplexer_5_out,
       pull_resistor_1_node, register_1_q, register_2_q;
  wire [7:1] undriven;

  Decoder #(.select(5), .enable("false")) decoder_1 (
    .out1(decoder_1_out1), .out2(decoder_1_out2), .out3(decoder_1_out3), .out4(decoder_1_out4),
    .out5(decoder_1_out5), .out6(decoder_1_out6), .out7(decoder_1_out7), .out8(decoder_1_out8),
    .out9(decoder_1_out9), .out10(Program_counter_increment), .out11(decoder_1_out11),
    .out12(decoder_1_out12), .out13(decoder_1_out13), .out14(decoder_1_out14), .out15(decoder_1_out15),
    .sel(Microcode[4:0]));  // open: out0, out16, out17, out18, out19, out20, out21, out22, out23, out24, out25, out26, out27, out28, out29, out30, out31
  Multiplexer #(.width(8), .enable("false")) multiplexer_1 (
    .in0(Parameter), .in1({undriven, Cin_Bin}), .out(multiplexer_1_out), .sel(decoder_1_out8));
  assign controlled_buffer_1_out = s_r_ff_1_qn ? decoder_1_out9 : 1'bz;  // Controlled_Buffer controlled_buffer_1
  Pull_Resistor pull_resistor_1 (.node(pull_resistor_1_node));
  Multiplexer #(.width(8), .enable("false")) multiplexer_2 (
    .in0(Bus_in), .in1(multiplexer_1_out), .out(pull_resistor_1_node), .sel(or_1_out));
  or or_1 (or_1_out, decoder_1_out8, decoder_1_out3);
  not not_1 (not_1_out, decoder_1_out2);
  Pull_Resistor pull_resistor_2 (.node(controlled_buffer_1_out));
  S_R_Flip_Flop s_r_ff_1 (
    .S(controlled_buffer_1_out), .clk(or_2_out), .R(Interrupt), .Q(Waiting), .Qn(s_r_ff_1_qn), .reset(Clear));  // open: preset, en
  or or_2 (or_2_out, controlled_buffer_1_out, Interrupt);
  Adder adder_1 (.a(Address), .b(8'h1), .out(adder_1_out));  // open: cin, cout
  Comparator comparator_1 (.a(Bus_in), .b({8{1'b0}}), .eq(comparator_1_eq));  // open: gt, lt
  not not_2 (not_2_out, decoder_1_out11);
  Register register_1 (.D(pull_resistor_1_node), .en(not_1_out), .Q(register_1_q), .clk(Clock_out), .clr(Clear));
  assign Bus_out = not_3_out ? register_1_q : 8'bz;  // Controlled_Buffer controlled_buffer_2
  not not_3 (not_3_out, Register_read);
  and and_1 (Clock_out, Clock, ~Interrupt, s_r_ff_1_qn);  // AND_Gate
  Register register_2 (.D(adder_1_out), .en(not_2_out), .Q(register_2_q), .clk(decoder_1_out12), .clr(Clear));
  Multiplexer #(.width(8), .enable("false")) multiplexer_3 (
    .in0(Parameter), .in1(Bus_in), .out(multiplexer_3_out), .sel(decoder_1_out7));
  Multiplexer #(.width(8), .enable("false")) multiplexer_4 (
    .in0(multiplexer_3_out), .in1(register_2_q), .out(multiplexer_4_out), .sel(decoder_1_out11));
  not not_4 (not_4_out, comparator_1_eq);
  assign Microcode_jump_address = Microcode_jump ? multiplexer_4_out : 8'bz;  // Controlled_Buffer controlled_buffer_3
  or JMP (Microcode_jump, 1'b0, controlled_buffer_4_out, controlled_buffer_5_out, decoder_1_out12, decoder_1_out6, decoder_1_out7, decoder_1_out11);
  assign controlled_buffer_4_out = comparator_1_eq ? decoder_1_out4 : 1'bz;  // Controlled_Buffer controlled_buffer_4
  assign controlled_buffer_5_out = not_4_out ? decoder_1_out5 : 1'bz;  // Controlled_Buffer controlled_buffer_5
  or RD (Register_read, decoder_1_out1, decoder_1_out14);
  or WR (Register_write, decoder_1_out2, decoder_1_out15);
  Multiplexer #(.width(8), .enable("false")) multiplexer_5 (
    .in0(Parameter), .in1(Bus_in), .out(multiplexer_5_out), .sel(decoder_1_out13));
  Register #(.trigger("high")) register_3 (
    .D(multiplexer_5_out), .Q(Register_select), .clk(RS_out), .clr(Clear));  // open: en
  or RS (RS_out, decoder_1_out1, decoder_1_out13, decoder_1_out2);
  Pull_Resistor pull_resistor_3 (.node(Microcode_jump_address));
  Pull_Resistor pull_resistor_4 (.node(Clock_out));
  Pull_Resistor pull_resistor_5 (.node(Register_select));
  Pull_Resistor pull_resistor_6 (.node(Bus_out));
  Pull_Resistor pull_resistor_7 (.node(controlled_buffer_4_out));
  Pull_Resistor pull_resistor_8 (.node(controlled_buffer_5_out));
  Pull_Resistor pull_resistor_9 (.node(decoder_1_out6));
  Pull_Resistor pull_resistor_10 (.node(decoder_1_out7));
  Pull_Resistor pull_resistor_11 (.node(decoder_1_out11));

  // Notes on the sheet:
  //   Clear: pull=down
  //   Clock: pull=down
  //   Cin_Bin: pull=down
  //   Interrupt: pull=down
  //   Parameter: pull=down
  //   Bus_in: pull=down
  //   Microcode: pull=down
endmodule

module RRD (
  input  [7:0] Register_value,
  input  [7:0] Register_address,
  input  [7:0] Select,
  input  Global_read,
  output [7:0] Bus_out,
  output Is_reading
);

  wire comparator_1_eq;

  Comparator comparator_1 (.a(Register_address), .b(Select), .eq(comparator_1_eq));  // open: gt, lt
  and and_1 (Is_reading, comparator_1_eq, Global_read);
  assign Bus_out = Is_reading ? Register_value : 8'bz;  // Controlled_Buffer controlled_buffer_1
endmodule

module EQU (
  input  [7:0] A,
  input  [7:0] B,
  input  E,
  output E_2
);

  wire comparator_1_eq;

  Comparator comparator_1 (.a(A), .b(B), .eq(comparator_1_eq));  // open: gt, lt
  and and_1 (E_2, comparator_1_eq, E);
endmodule

module REG (
  input  [7:0] Register_select,
  input  [7:0] Start,
  input  [7:0] Bus,
  input  Write,
  input  Clear,
  input  Read,
  input  Clear2,
  output [7:0] Out,
  output Reading
);

  wire equ_1_e_2, equ_2_e_2, equ_3_e_2, equ_4_e_2, or_1_out, rrd_1_is_reading, rrd_2_is_reading,
       rrd_3_is_reading, rrd_4_is_reading;
  wire [7:0] register_1_q, register_2_q, register_3_q, register_4_q, rrd_1_bus_out;

  or or_1 (or_1_out, Clear2, Clear);
  EQU equ_1 (.A(Register_select), .B({Start[7:2], 2'b00}), .E(Write), .E_2(equ_1_e_2));
  EQU equ_2 (.A(Register_select), .B({Start[7:2], 2'b01}), .E(Write), .E_2(equ_2_e_2));
  EQU equ_3 (.A(Register_select), .B({Start[7:2], 2'b10}), .E(Write), .E_2(equ_3_e_2));
  EQU equ_4 (.A(Register_select), .B({Start[7:2], 2'b11}), .E(Write), .E_2(equ_4_e_2));
  Register register_1 (.D(Bus), .Q(register_1_q), .clk(equ_1_e_2), .clr(or_1_out));  // open: en
  Register register_2 (.D(Bus), .Q(register_2_q), .clk(equ_2_e_2), .clr(or_1_out));  // open: en
  Register register_3 (.D(Bus), .Q(register_3_q), .clk(equ_3_e_2), .clr(or_1_out));  // open: en
  Register register_4 (.D(Bus), .Q(register_4_q), .clk(equ_4_e_2), .clr(or_1_out));  // open: en
  RRD rrd_1 (
    .Register_value(register_1_q), .Register_address({Start[7:2], 2'b00}), .Select(Register_select),
    .Global_read(Read), .Bus_out(rrd_1_bus_out), .Is_reading(rrd_1_is_reading));
  RRD rrd_2 (
    .Register_value(register_2_q), .Register_address({Start[7:2], 2'b01}), .Select(Register_select),
    .Global_read(Read), .Bus_out(rrd_1_bus_out), .Is_reading(rrd_2_is_reading));
  RRD rrd_3 (
    .Register_value(register_3_q), .Register_address({Start[7:2], 2'b10}), .Select(Register_select),
    .Global_read(Read), .Bus_out(rrd_1_bus_out), .Is_reading(rrd_3_is_reading));
  RRD rrd_4 (
    .Register_value(register_4_q), .Register_address({Start[7:2], 2'b11}), .Select(Register_select),
    .Global_read(Read), .Bus_out(rrd_1_bus_out), .Is_reading(rrd_4_is_reading));
  or or_2 (Reading, rrd_1_is_reading, rrd_2_is_reading, rrd_3_is_reading, rrd_4_is_reading);
  assign Out = Reading ? rrd_1_bus_out : 8'bz;  // Controlled_Buffer controlled_buffer_1

  // Notes on the sheet:
  //   Clear2: pull=down
  //   Microcode registers
  //   Used by the microcode to store shit, like the GPR but for the microcode
endmodule

module MCTR (
  input  [15:0] Data,
  input  [7:0] Address,
  input  Jump,
  input  Clock,
  input  Reset,
  input  [7:0] MIP_Address,
  input  [7:0] Register,
  input  Read,
  output [7:0] Instruction,
  output [7:0] Parameter,
  output [7:0] Address_2,
  output [7:0] MIP_plus_plus,
  output Reading
);

  wire not_1_out;

  Counter counter_1 (
    .load(Jump), .D(Address), .count(not_1_out), .Q(Address_2), .clk(Clock), .clr(Reset));  // open: carry
  not not_1 (not_1_out, Jump);
  Adder adder_1 (.a(Address_2), .b(8'h1), .out(MIP_plus_plus));  // open: cin, cout
  EQU equ_1 (.A(MIP_Address), .B(Register), .E(Read), .E_2(Reading));

  assign Instruction = Data[15:8];
  assign Parameter = Data[7:0];
endmodule

module RBUF (
  input  [7:0] Data_in,
  input  [7:0] Register_select,
  input  [7:0] Address,
  input  Write,
  input  Clear,
  output [7:0] Data_out
);

  wire equ_1_e_2;

  Register register_1 (.D(Data_in), .Q(Data_out), .clk(equ_1_e_2), .clr(Clear));  // open: en
  EQU equ_1 (.A(Address), .B(Register_select), .E(Write), .E_2(equ_1_e_2));
endmodule

module Entry (
  input  _0,
  input  _1,
  input  _2,
  input  _3,
  input  _4,
  input  _5,
  input  _6,
  input  _7,
  input  Zero_all,
  input  Enable,
  input  One_all,
  output [7:0] Value,
  output _0_2,
  output _1_2,
  output _2_2,
  output _3_2,
  output _4_2,
  output _5_2,
  output _6_2,
  output _7_2
);

  T_Flip_Flop t_ff_1 (.clk(_0), .T(_0), .Q(_0_2), .preset(One_all), .reset(Zero_all), .en(Enable));  // open: Qn
  T_Flip_Flop t_ff_2 (.clk(_1), .T(_1), .Q(_1_2), .preset(One_all), .reset(Zero_all), .en(Enable));  // open: Qn
  T_Flip_Flop t_ff_3 (.clk(_2), .T(_2), .Q(_2_2), .preset(One_all), .reset(Zero_all), .en(Enable));  // open: Qn
  T_Flip_Flop t_ff_4 (.clk(_4), .T(_4), .Q(_4_2), .preset(One_all), .reset(Zero_all), .en(Enable));  // open: Qn
  T_Flip_Flop t_ff_5 (.clk(_3), .T(_3), .Q(_3_2), .preset(One_all), .reset(Zero_all), .en(Enable));  // open: Qn
  T_Flip_Flop t_ff_6 (.clk(_5), .T(_5), .Q(_5_2), .preset(One_all), .reset(Zero_all), .en(Enable));  // open: Qn
  T_Flip_Flop t_ff_7 (.clk(_6), .T(_6), .Q(_6_2), .preset(One_all), .reset(Zero_all), .en(Enable));  // open: Qn
  T_Flip_Flop t_ff_8 (.clk(_7), .T(_7), .Q(_7_2), .preset(One_all), .reset(Zero_all), .en(Enable));  // open: Qn
  Pull_Resistor pull_resistor_1 (.node(Zero_all));
  Pull_Resistor #(.pull(1)) pull_resistor_2 (.node(Enable));
  Pull_Resistor pull_resistor_3 (.node(One_all));

  assign Value = {_0_2, _1_2, _2_2, _3_2, _4_2, _5_2, _6_2, _7_2};

  // Notes on the sheet:
  //   One_all: pull=down
  //   Enable: pull=up
  //   Zero_all: pull=down
endmodule

module CmpPass (
  input  [7:0] A,
  input  [7:0] B,
  input  _1__or____0,
  output [7:0] Out
);

  wire comparator_1_lt, multiplexer_1_out, not_1_out;

  Comparator #(.mode("unsigned")) comparator_1 (.a(B), .b(A), .lt(comparator_1_lt));  // open: gt, eq
  Multiplexer #(.enable("false")) multiplexer_1 (
    .in0(comparator_1_lt), .in1(not_1_out), .out(multiplexer_1_out), .sel(_1__or____0));
  not not_1 (not_1_out, comparator_1_lt);
  Multiplexer #(.width(8), .enable("false")) multiplexer_2 (.in0(A), .in1(B), .out(Out), .sel(multiplexer_1_out));
endmodule

// Logic
module ALU_LOGIC (
  input  [7:0] A,
  input  [7:0] B,
  output [7:0] A_2,
  output [7:0] B_2,
  output [7:0] NOT_A,
  output [7:0] NOT_B,
  output [7:0] AND,
  output [7:0] OR,
  output [7:0] XOR,
  output [7:0] IMPLY_A,
  output [7:0] IMPLY_B,
  output [7:0] Pass_lesser,
  output [7:0] Pass_greater
);

  wire comparator_1_lt, comparator_2_lt, not_3_out;

  assign NOT_A = ~A;  // NOT_Gate not_1, 8 bits wide
  assign NOT_B = ~B;  // NOT_Gate not_2, 8 bits wide
  assign AND = A & B;  // AND_Gate and_1, 8 bits wide
  assign OR = A | B;  // OR_Gate or_1, 8 bits wide
  assign XOR = A ^ B;  // XOR_Gate xor_1, 8 bits wide
  assign IMPLY_A = ~A | B;  // OR_Gate or_2, 8 bits wide
  assign IMPLY_B = A | ~B;  // OR_Gate or_3, 8 bits wide
  not not_3 (not_3_out, comparator_1_lt);
  Comparator #(.mode("unsigned")) comparator_1 (.a(A), .b(B), .lt(comparator_1_lt));  // open: gt, eq
  Comparator #(.mode("unsigned")) comparator_2 (.a(A), .b(B), .lt(comparator_2_lt));  // open: gt, eq
  Multiplexer #(.width(8), .enable("false")) multiplexer_1 (.in0(A), .in1(B), .out(Pass_lesser), .sel(not_3_out));
  Multiplexer #(.width(8), .enable("false")) multiplexer_2 (
    .in0(A), .in1(B), .out(Pass_greater), .sel(comparator_2_lt));

  assign A_2 = A;
  assign B_2 = B;
endmodule

// ALU
module ALU_NEW (
  input  [7:0] Data,
  input  [7:0] Register_select,
  input  Global_write,
  input  Global_read,
  input  Clear,
  output [7:0] Output,
  output Reading,
  output Cout_Bout
);

  wire comparator_1_eq, comparator_2_eq, comparator_3_eq, controlled_buffer_1_out, equ_1_e_2, equ_2_e_2,
       equ_3_e_2, pull_resistor_2_node, pull_resistor_3_node;
  wire [2:0] alu_arith_1_cout_bout1_bout2;
  wire [7:0] alu_arith_1_a___b, alu_arith_1_a___b_2, alu_arith_1_b___a, alu_arith_1_left_shift_a_by_b,
       alu_arith_1_minus_a, alu_arith_1_minus_b, alu_arith_1_right_shift_a_by_b,
       alu_arith_1_rotate_a_left_by_b, alu_arith_1_rotate_a_right_by_b, alu_arith_1_select_bit_b_from_a,
       alu_logic_1_a_2, alu_logic_1_and, alu_logic_1_b_2, alu_logic_1_imply_a, alu_logic_1_imply_b,
       alu_logic_1_not_a, alu_logic_1_not_b, alu_logic_1_or, alu_logic_1_pass_greater,
       alu_logic_1_pass_lesser, alu_logic_1_xor, multiplexer_1_out, multiplexer_2_out, multiplexer_3_out,
       not_1_out, register_1_q, register_2_q, register_3_q, shifter_1_out, shifter_2_out, shifter_3_out;

  EQU equ_1 (.A(Register_select), .B(8'h10), .E(Global_write), .E_2(equ_1_e_2));
  EQU equ_2 (.A(Register_select), .B(8'h11), .E(Global_write), .E_2(equ_2_e_2));
  EQU equ_3 (.A(Register_select), .B(8'h12), .E(Global_write), .E_2(equ_3_e_2));
  EQU equ_4 (.A(Register_select), .B(8'h13), .E(Global_read), .E_2(Reading));
  Register register_1 (.D(Data), .Q(register_1_q), .clk(equ_1_e_2), .clr(Clear));  // open: en
  Register register_2 (.D(Data), .Q(register_2_q), .clk(equ_2_e_2), .clr(Clear));  // open: en
  Register register_3 (.D(Data), .Q(register_3_q), .clk(equ_3_e_2), .clr(Clear));  // open: en
  ALU_LOGIC alu_logic_1 (
    .A(register_1_q), .B(register_2_q), .A_2(alu_logic_1_a_2), .B_2(alu_logic_1_b_2),
    .NOT_A(alu_logic_1_not_a), .NOT_B(alu_logic_1_not_b), .AND(alu_logic_1_and), .OR(alu_logic_1_or),
    .XOR(alu_logic_1_xor), .IMPLY_A(alu_logic_1_imply_a), .IMPLY_B(alu_logic_1_imply_b),
    .Pass_lesser(alu_logic_1_pass_lesser), .Pass_greater(alu_logic_1_pass_greater));
  ALU_ARITH alu_arith_1 (
    .A(register_1_q), .B(register_2_q), .Cout_Bout1_Bout2(alu_arith_1_cout_bout1_bout2),
    .A___B(alu_arith_1_a___b), .A___B_2(alu_arith_1_a___b_2), .B___A(alu_arith_1_b___a),
    .minus_A(alu_arith_1_minus_a), .minus_B(alu_arith_1_minus_b),
    .Left_shift_A_by_B(alu_arith_1_left_shift_a_by_b), .Right_shift_A_by_B(alu_arith_1_right_shift_a_by_b),
    .Rotate_A_left_by_B(alu_arith_1_rotate_a_left_by_b),
    .Rotate_A_right_by_B(alu_arith_1_rotate_a_right_by_b),
    .Select_bit_B_from_A(alu_arith_1_select_bit_b_from_a));
  Multiplexer #(.select(5), .width(8), .enable("false")) multiplexer_1 (
    .in0(alu_logic_1_a_2), .in1(alu_logic_1_b_2), .in2(alu_logic_1_not_a), .in3(alu_logic_1_not_b),
    .in4(alu_logic_1_and), .in5(alu_logic_1_or), .in6(alu_logic_1_xor), .in7(alu_logic_1_imply_a),
    .in8(alu_logic_1_imply_b), .in9(alu_logic_1_pass_lesser), .in10(alu_logic_1_pass_greater),
    .in11({8{1'b1}}), .in12({8{1'b0}}), .in13(alu_arith_1_a___b), .in14(alu_arith_1_a___b_2),
    .in15(alu_arith_1_b___a), .in16(alu_arith_1_minus_a), .in17(alu_arith_1_minus_b),
    .in18(alu_arith_1_left_shift_a_by_b), .in19(alu_arith_1_right_shift_a_by_b),
    .in20(alu_arith_1_rotate_a_left_by_b), .in21(alu_arith_1_rotate_a_right_by_b),
    .in22(alu_arith_1_select_bit_b_from_a), .out(multiplexer_1_out), .sel(register_3_q[4:0]));  // open: in23, in24, in25, in26, in27, in28, in29, in30, in31
  Shifter #(.shift("ar")) shifter_1 (.in(multiplexer_1_out), .\dist (3'b001), .out(shifter_1_out));
  Shifter shifter_2 (.in(multiplexer_1_out), .\dist (3'b001), .out(shifter_2_out));
  Shifter #(.shift("lr")) shifter_3 (.in(multiplexer_1_out), .\dist (3'b001), .out(shifter_3_out));
  Comparator #(.width(5), .mode("unsigned")) comparator_1 (
    .a(register_3_q[4:0]), .b(5'b01101), .eq(comparator_1_eq));  // open: gt, lt
  Comparator #(.width(5), .mode("unsigned")) comparator_2 (
    .a(register_3_q[4:0]), .b(5'b01110), .eq(comparator_2_eq));  // open: gt, lt
  Comparator #(.width(5), .mode("unsigned")) comparator_3 (
    .a(register_3_q[4:0]), .b(5'b01111), .eq(comparator_3_eq));  // open: gt, lt
  Multiplexer #(.select(2), .width(8), .enable("false")) multiplexer_2 (
    .in0(multiplexer_1_out), .in1(shifter_1_out), .in2(shifter_2_out), .in3(shifter_3_out),
    .out(multiplexer_2_out), .sel(register_3_q[6:5]));
  assign not_1_out = ~multiplexer_2_out;  // NOT_Gate not_1, 8 bits wide
  or or_1 (Cout_Bout, controlled_buffer_1_out, pull_resistor_2_node, pull_resistor_3_node);
  assign controlled_buffer_1_out = comparator_1_eq ? alu_arith_1_cout_bout1_bout2[0] : 1'bz;  // Controlled_Buffer controlled_buffer_1
  Pull_Resistor pull_resistor_1 (.node(controlled_buffer_1_out));
  Pull_Resistor pull_resistor_2 (.node(pull_resistor_2_node));
  Pull_Resistor pull_resistor_3 (.node(pull_resistor_3_node));
  assign pull_resistor_2_node = comparator_2_eq ? alu_arith_1_cout_bout1_bout2[1] : 1'bz;  // Controlled_Buffer controlled_buffer_2
  assign pull_resistor_3_node = comparator_3_eq ? alu_arith_1_cout_bout1_bout2[2] : 1'bz;  // Controlled_Buffer controlled_buffer_3
  assign Output = Reading ? multiplexer_3_out : 8'bz;  // Controlled_Buffer controlled_buffer_4
  Multiplexer #(.width(8), .enable("false")) multiplexer_3 (
    .in0(multiplexer_2_out), .in1(not_1_out), .out(multiplexer_3_out), .sel(register_3_q[7]));

  // Other names for the same wires on the sheet: R = Reading

  // Notes on the sheet:
  //   Cout_Bout: pull=down
  //   A
  //   B
  //   OPC
  //   OUT
endmodule

// Arith
module ALU_ARITH (
  input  [7:0] A,
  input  [7:0] B,
  output [2:0] Cout_Bout1_Bout2,
  output [7:0] A___B,
  output [7:0] A___B_2,
  output [7:0] B___A,
  output [7:0] minus_A,
  output [7:0] minus_B,
  output [7:0] Left_shift_A_by_B,
  output [7:0] Right_shift_A_by_B,
  output [7:0] Rotate_A_left_by_B,
  output [7:0] Rotate_A_right_by_B,
  output [7:0] Select_bit_B_from_A
);

  Adder adder_1 (.a(A), .b(B), .out(A___B), .cout(Cout_Bout1_Bout2[0]));  // open: cin
  Subtractor subtractor_1 (.a(A), .b(B), .out(A___B_2), .bout(Cout_Bout1_Bout2[1]));  // open: bin
  Subtractor subtractor_2 (.a(B), .b(A), .out(B___A), .bout(Cout_Bout1_Bout2[2]));  // open: bin
  Negator negator_1 (.in(A), .out(minus_A));
  Negator negator_2 (.in(B), .out(minus_B));
  Shifter shifter_1 (.in(A), .\dist (B[2:0]), .out(Left_shift_A_by_B));
  Shifter #(.shift("lr")) shifter_2 (.in(A), .\dist (B[2:0]), .out(Right_shift_A_by_B));
  Shifter #(.shift("rl")) shifter_3 (.in(A), .\dist (B[2:0]), .out(Rotate_A_left_by_B));
  Shifter #(.shift("rr")) shifter_4 (.in(A), .\dist (B[2:0]), .out(Rotate_A_right_by_B));
  BitSelector bitselector_1 (.in(A), .out(Select_bit_B_from_A[0]), .sel(B[2:0]));
endmodule

// REG
module REG_BANK (
  input  [7:0] Bus_in,
  input  [7:0] Register_select,
  input  Write,
  input  Read,
  input  Clear,
  input  PCI,
  output [7:0] Out,
  output Is_reading
);

  wire reg_1_reading, reg_2_reading, reg_3_reading, reg_4_reading, reg_5_reading, reg_6_reading;
  wire [7:0] reg_1_out;

  REG reg_1 (
    .Register_select(Register_select), .Bus(Bus_in), .Write(Write), .Clear(Clear), .Read(Read),
    .Out(reg_1_out), .Reading(reg_1_reading), .Clear2(PCI), .Start(8'h20));
  REG reg_2 (
    .Register_select(Register_select), .Bus(Bus_in), .Write(Write), .Clear(Clear), .Read(Read),
    .Out(reg_1_out), .Reading(reg_2_reading), .Clear2(1'b0), .Start(8'h24));
  REG reg_3 (
    .Register_select(Register_select), .Bus(Bus_in), .Write(Write), .Clear(Clear), .Read(Read),
    .Out(reg_1_out), .Reading(reg_3_reading), .Clear2(1'b0), .Start(8'h30));
  REG reg_4 (
    .Register_select(Register_select), .Bus(Bus_in), .Write(Write), .Clear(Clear), .Read(Read),
    .Out(reg_1_out), .Reading(reg_4_reading), .Clear2(1'b0), .Start(8'h34));
  REG reg_5 (
    .Register_select(Register_select), .Bus(Bus_in), .Write(Write), .Clear(Clear), .Read(Read),
    .Out(reg_1_out), .Reading(reg_5_reading), .Clear2(1'b0), .Start(8'h38));
  REG reg_6 (
    .Register_select(Register_select), .Bus(Bus_in), .Write(Write), .Clear(Clear), .Read(Read),
    .Out(reg_1_out), .Reading(reg_6_reading), .Clear2(1'b0), .Start(8'h3c));
  assign Out = Is_reading ? reg_1_out : 8'bz;  // Controlled_Buffer controlled_buffer_1
  or or_1 (Is_reading, reg_1_reading, reg_2_reading, reg_3_reading, reg_4_reading, reg_5_reading, reg_6_reading);
endmodule
